# Fritzing sketch robot_car (saved by Fritzing 1.0.8)

parts:
  C1_Pi_Zero_2_W = Raspberry Pi Zero
  B2_2S_LiPo_7_4_V = Battery [voltage=7.4V]
  F1_2_A = FUSE [package=fuse_5mm]
  SW1 = Toggle Switch [package=THT]
  P1_#1_5_1_V = MP1584EN buck module [output_voltage="5.1 V"]
  P1_#2_6_0_V = MP1584EN buck module [output_voltage="6.0 V"]
  D2 = DRV8833 breakout
  M2_left = DC Motor
  M2_right = DC Motor
  100_nF = Capacitor [package=cap-pth-small]
  100_nF_2 = Capacitor [package=cap-pth-small]

nets:
  N1: C1_Pi_Zero_2_W.pin_2, P1_#1_5_1_V.OUT+_1
  N2: C1_Pi_Zero_2_W.pin_6, C1_Pi_Zero_2_W.pin_34, B2_2S_LiPo_7_4_V.-, P1_#1_5_1_V.IN-_1, P1_#1_5_1_V.OUT-_1, P1_#2_6_0_V.IN-_1, P1_#2_6_0_V.OUT-_1, P1_#2_6_0_V.OUT-_2, D2.GND
  N3: C1_Pi_Zero_2_W.pin_32, D2.IN1
  N4: C1_Pi_Zero_2_W.pin_33, D2.IN2
  N5: C1_Pi_Zero_2_W.pin_35, D2.IN3
  N6: C1_Pi_Zero_2_W.pin_36, D2.IN4
  N7: B2_2S_LiPo_7_4_V.+, F1_2_A.1
  N8: F1_2_A.2, SW1.COM
  N9: SW1.L1, P1_#1_5_1_V.IN+_1, P1_#2_6_0_V.IN+_1
  N10: P1_#2_6_0_V.OUT+_1, D2.VCC
  N11: D2.OUT1, M2_left.pin_1, 100_nF.1
  N12: D2.OUT2, M2_left.pin_2, 100_nF.2
  N13: D2.OUT3, M2_right.pin_1, 100_nF_2.1
  N14: D2.OUT4, M2_right.pin_2, 100_nF_2.2

custom parts:
  MP1584EN buck module: MP1584EN adjustable step-down module (parts library P1), 22.5 x 17 mm. Each short edge has two pad pairs, and on the robot car each pair carries a 2-pin male header, so every net has two pins. IN- and OUT- are the same copper (no isolation). Input 4.5-28 V, output set by a single-turn trimpot. Schematic symbol only - no breadboard or PCB view.
  DRV8833 breakout: DRV8833 dual H-bridge breakout (parts library D2): 12 pins in two rows, labels on the face opposite the chip. The symbol's pin order follows the robot car's wiring, not the board; the board's own order is in parts/d2.html. Schematic symbol only - no breadboard or PCB view.
